# Fritzing sketch RcSwitchReceiverDue (saved by Fritzing 1.0.4)
circuit board: 6.88566cm x 5.36311cm

parts:
  Receiver = RF-LINK_RX [package=rf-link_rx]
  S1 = Pushbutton [package="[THT]"]
  D1 = Diode [package=diode-1n4148]
  Bauteil1 = Arduino Due (Rev2b)

nets:
  GND: Receiver.GND, S1.Pin_3, S1.Pin_4, Bauteil1.GND
  N1: Receiver.DATA, D1.C
  +5V: Receiver.+5V, Bauteil1.5V
  N2: S1.Pin_2, Bauteil1.D13_PWM
  N3: D1.A, Bauteil1.D6_PWM

notes:
  Diode avoids +5V on IO pin, which would damage Arduino Due
